// Logisim project Elevador_3_Andares_Final.circ as structural Verilog: 12 circuits, main circuit principal
module principal (
  output [2:0] out_1,
  output [2:0] Estado_Final
);

  wire clock_1_out, entradas_para_7_seg_1_a, entradas_para_7_seg_1_b, entradas_para_7_seg_1_c,
       entradas_para_7_seg_1_d, entradas_para_7_seg_1_e, entradas_para_7_seg_1_f, entradas_para_7_seg_1_g;
  wire [1:0] busca_de_yd_1_yd;
  wire [2:0] cod_prioridade_subida_1_q2__q1__q0, proximo_andar_1_proximo_estado,
       \seção_de_travamento_1_i2__i1__i0_2 , Terra_out;
  wire [3:0] _0U_out, entradas_para_seta_1_out_2, entradas_para_seta_1_out_3, entradas_para_seta_1_out_4,
       \seção_de_travamento_1_o2d__o1u__o1d__o0u_2 ;
  wire [4:0] Decodificador_y7__y6__y5__y4__y3;

  Button _2D (.out(_0U_out[3]));
  Button _1U (.out(_0U_out[2]));
  Button _1D (.out(_0U_out[1]));
  Button _0U (.out(_0U_out[0]));
  Button Segundo (.out(Terra_out[2]));
  Button Primeiro (.out(Terra_out[1]));
  Button Terra (.out(Terra_out[0]));
  \Seção_de_Travamento  \seção_de_travamento_1  (
    .O2d__O1u__O1d__O0u(_0U_out), .I2__I1__I0(Terra_out), .Yu__Yd(busca_de_yd_1_yd),
    .S2__S1__S0(Estado_Final), .O2d__O1u__O1d__O0u_2(\seção_de_travamento_1_o2d__o1u__o1d__o0u_2 ),
    .I2__I1__I0_2(\seção_de_travamento_1_i2__i1__i0_2 ));
  Busca_de_Yu busca_de_yu_1 (
    .O2d__O1u__O1d__O0u(\seção_de_travamento_1_o2d__o1u__o1d__o0u_2 ),
    .I2__I1__I0(\seção_de_travamento_1_i2__i1__i0_2 ), .S2__S1__S0(Estado_Final),
    .Yu__Yd_Atuais(busca_de_yd_1_yd), .Yu(busca_de_yd_1_yd[1]));
  Busca_de_Yd busca_de_yd_1 (
    .O2d__O1u__O1d__O0u(\seção_de_travamento_1_o2d__o1u__o1d__o0u_2 ),
    .I2__I1__I0(\seção_de_travamento_1_i2__i1__i0_2 ), .S2__S1__S0(Estado_Final),
    .Yu__Yd_Atuais(busca_de_yd_1_yd), .Yd(busca_de_yd_1_yd[0]));
  Cod_Prioridade_Subida cod_prioridade_subida_1 (
    .O2d__O1u__O1d__O0u(\seção_de_travamento_1_o2d__o1u__o1d__o0u_2 ),
    .I2__I1__I0(\seção_de_travamento_1_i2__i1__i0_2 ), .Yu__Yd(busca_de_yd_1_yd),
    .Q2__Q1__Q0(cod_prioridade_subida_1_q2__q1__q0));
  Cod_Prioridade_Descida cod_prioridade_descida_1 (
    .O2d__O1u__O1d__O0u(\seção_de_travamento_1_o2d__o1u__o1d__o0u_2 ),
    .I2__I1__I0(\seção_de_travamento_1_i2__i1__i0_2 ), .Yu__Yd(busca_de_yd_1_yd),
    .Q2__Q1__Q0(cod_prioridade_subida_1_q2__q1__q0));
  \Cálculo_de_Estado  \Cálculo_de_Estado  (
    .Y7__Y6__Y5__Y4__Y3(Decodificador_y7__y6__y5__y4__y3), .Yu__Yd(busca_de_yd_1_yd),
    .Estado_Antigo(Estado_Final), .S2__S1__S0(out_1));
  Decodificador Decodificador (
    .Q2__Q1__Q0(cod_prioridade_subida_1_q2__q1__q0), .Y7__Y6__Y5__Y4__Y3(Decodificador_y7__y6__y5__y4__y3));
  Register #(.width(3)) Atraso (
    .D(proximo_andar_1_proximo_estado), .Q(Estado_Final), .clk(clock_1_out));  // open: en, clr
  Clock clock_1 (.out(clock_1_out));
  Entradas_para_7_Seg entradas_para_7_seg_1 (
    .S2__S1__S0(Estado_Final), .a(entradas_para_7_seg_1_a), .b(entradas_para_7_seg_1_b),
    .c(entradas_para_7_seg_1_c), .d(entradas_para_7_seg_1_d), .e(entradas_para_7_seg_1_e),
    .f(entradas_para_7_seg_1_f), .g(entradas_para_7_seg_1_g));
  Entradas_para_Seta entradas_para_seta_1 (
    .Yu__Yd(busca_de_yd_1_yd), .out_2(entradas_para_seta_1_out_2), .out_3(entradas_para_seta_1_out_3),
    .out_4(entradas_para_seta_1_out_4));
  Proximo_Andar proximo_andar_1 (
    .Estado_Atual(Estado_Final), .Destino(out_1), .Proximo_Estado(proximo_andar_1_proximo_estado));
  _7_Segment_Display u_7_segment_display_1 (
    .g(entradas_para_7_seg_1_g), .f(entradas_para_7_seg_1_f), .a(entradas_para_7_seg_1_a),
    .b(entradas_para_7_seg_1_b), .e(entradas_para_7_seg_1_e), .d(entradas_para_7_seg_1_d),
    .c(entradas_para_7_seg_1_c));  // open: dp
  DotMatrix #(.matrixcols(3), .matrixrows(4), .dotshape("circle")) dotmatrix_1 (
    .col0(entradas_para_seta_1_out_2), .col1(entradas_para_seta_1_out_3), .col2(entradas_para_seta_1_out_4));

  // Notes on the sheet:
  //   De fora
  //   De dentro
  //   Seção de Travamento
  //   Unidade de Controle Direcional
  //   Controlador de Subida
  //   Controlador de Descida
  //   Display de Saída
  //   Direção
endmodule

module \Seção_de_Travamento  (
  input  [3:0] O2d__O1u__O1d__O0u,
  input  [2:0] I2__I1__I0,
  input  [1:0] Yu__Yd,
  input  [2:0] S2__S1__S0,
  output [3:0] O2d__O1u__O1d__O0u_2,
  output [2:0] I2__I1__I0_2
);

  wire and_1_out, and_2_out;

  and and_1 (and_1_out, ~Yu__Yd[0], S2__S1__S0[1]);  // AND_Gate
  and and_2 (and_2_out, ~Yu__Yd[1], S2__S1__S0[1]);  // AND_Gate
  J_K_Flip_Flop j_k_ff_1 (
    .J(1'b1), .clk(O2d__O1u__O1d__O0u[3]), .K(1'b1), .Q(O2d__O1u__O1d__O0u_2[3]), .reset(S2__S1__S0[2]));  // open: Qn, preset, en
  J_K_Flip_Flop j_k_ff_2 (
    .J(1'b1), .clk(O2d__O1u__O1d__O0u[2]), .K(1'b1), .Q(O2d__O1u__O1d__O0u_2[2]), .reset(and_1_out));  // open: Qn, preset, en
  J_K_Flip_Flop j_k_ff_3 (
    .J(1'b1), .clk(O2d__O1u__O1d__O0u[1]), .K(1'b1), .Q(O2d__O1u__O1d__O0u_2[1]), .reset(and_2_out));  // open: Qn, preset, en
  J_K_Flip_Flop j_k_ff_4 (
    .J(1'b1), .clk(O2d__O1u__O1d__O0u[0]), .K(1'b1), .Q(O2d__O1u__O1d__O0u_2[0]), .reset(S2__S1__S0[0]));  // open: Qn, preset, en
  J_K_Flip_Flop j_k_ff_5 (
    .J(1'b1), .clk(I2__I1__I0[2]), .K(1'b1), .Q(I2__I1__I0_2[2]), .reset(S2__S1__S0[2]));  // open: Qn, preset, en
  J_K_Flip_Flop j_k_ff_6 (
    .J(1'b1), .clk(I2__I1__I0[1]), .K(1'b1), .Q(I2__I1__I0_2[1]), .reset(S2__S1__S0[1]));  // open: Qn, preset, en
  J_K_Flip_Flop j_k_ff_7 (
    .J(1'b1), .clk(I2__I1__I0[0]), .K(1'b1), .Q(I2__I1__I0_2[0]), .reset(S2__S1__S0[0]));  // open: Qn, preset, en
endmodule

module Mux_para_Estado (
  input  [2:0] S2__S1__S0,
  input  [1:0] Yu__Yd,
  input  [2:0] Estado_Antigo,
  output [2:0] \Estado_de_Saída 
);

  wire [1:0] and_2_out;
  wire [2:0] undriven;

  and and_1 (and_2_out[1], ~Yu__Yd[0], ~Yu__Yd[1]);  // AND_Gate
  and and_2 (and_2_out[0], ~Estado_Antigo[0], ~Estado_Antigo[1], ~Estado_Antigo[2]);  // AND_Gate
  Multiplexer #(.select(2), .width(3)) multiplexer_1 (
    .in0(S2__S1__S0), .in1(undriven), .in2(Estado_Antigo), .in3(3'b001), .out(\Estado_de_Saída ),
    .sel(and_2_out));  // open: en

  // Notes on the sheet:
  //   Estado Calculado
  //   001
endmodule

module \Cálculo_de_Estado  (
  input  [1:0] Yu__Yd,
  input  [4:0] Y7__Y6__Y5__Y4__Y3,
  input  [2:0] Estado_Antigo,
  output [2:0] S2__S1__S0
);

  wire or_1_out, or_2_out, or_3_out, Yd_Yu_prime_out, Yu_Yd_prime_out;
  wire [2:0] and_1_out;

  and Yd_Yu_prime (Yd_Yu_prime_out, Yu__Yd[0], ~Yu__Yd[1]);  // AND_Gate
  and Yu_Yd_prime (Yu_Yd_prime_out, Yu__Yd[1], ~Yu__Yd[0]);  // AND_Gate
  or or_1 (or_1_out, Yu_Yd_prime_out, Yd_Yu_prime_out);
  or or_2 (or_2_out, Y7__Y6__Y5__Y4__Y3[1], Y7__Y6__Y5__Y4__Y3[2]);
  or or_3 (or_3_out, Y7__Y6__Y5__Y4__Y3[3], Y7__Y6__Y5__Y4__Y3[0], Y7__Y6__Y5__Y4__Y3[4]);
  and and_1 (and_1_out[0], Yd_Yu_prime_out, or_2_out);
  and and_2 (and_1_out[1], or_1_out, or_3_out);
  and and_3 (and_1_out[2], Yu_Yd_prime_out, or_2_out);
  Mux_para_Estado mux_para_estado_1 (
    .S2__S1__S0(and_1_out), .Yu__Yd(Yu__Yd), .Estado_Antigo(Estado_Antigo), .\Estado_de_Saída (S2__S1__S0));

  // Notes on the sheet:
  //   Variáveis de Direção
  //   Saídas do Decodificador
  //   Xnor(Yu, Yd)
  //   Y4 + Y5
  //   Y3 + Y6 + Y7
endmodule

module Cod_Prioridade_Subida (
  input  [3:0] O2d__O1u__O1d__O0u,
  input  [2:0] I2__I1__I0,
  input  [1:0] Yu__Yd,
  output [2:0] Q2__Q1__Q0
);

  wire and_1_out;

  Priority_Encoder priority_encoder_1 (
    .in0(1'b1), .in1(1'b1), .in2(1'b1), .in3(O2d__O1u__O1d__O0u[1]), .in4(O2d__O1u__O1d__O0u[3]),
    .in5(I2__I1__I0[2]), .in6(O2d__O1u__O1d__O0u[2]), .in7(I2__I1__I0[1]), .out(Q2__Q1__Q0), .en_in(and_1_out));  // open: gs, en_out
  and and_1 (and_1_out, Yu__Yd[1], ~Yu__Yd[0]);  // AND_Gate

  // Notes on the sheet:
  //   O1d, O2d, I2, O1u, I1
endmodule

module Cod_Prioridade_Descida (
  input  [3:0] O2d__O1u__O1d__O0u,
  input  [2:0] I2__I1__I0,
  input  [1:0] Yu__Yd,
  output [2:0] Q2__Q1__Q0
);

  wire and_1_out;

  Priority_Encoder priority_encoder_1 (
    .in0(1'b1), .in1(1'b1), .in2(1'b1), .in3(O2d__O1u__O1d__O0u[2]), .in4(O2d__O1u__O1d__O0u[0]),
    .in5(I2__I1__I0[0]), .in6(O2d__O1u__O1d__O0u[1]), .in7(I2__I1__I0[1]), .out(Q2__Q1__Q0), .en_in(and_1_out));  // open: gs, en_out
  and and_1 (and_1_out, ~Yu__Yd[1], Yu__Yd[0]);  // AND_Gate

  // Notes on the sheet:
  //   O1u, O0u, I0, O1d, I1
endmodule

module Decodificador (
  input  [2:0] Q2__Q1__Q0,
  output [4:0] Y7__Y6__Y5__Y4__Y3
);

  Decoder #(.select(3)) decoder_1 (
    .out3(Y7__Y6__Y5__Y4__Y3[0]), .out4(Y7__Y6__Y5__Y4__Y3[1]), .out5(Y7__Y6__Y5__Y4__Y3[2]),
    .out6(Y7__Y6__Y5__Y4__Y3[3]), .out7(Y7__Y6__Y5__Y4__Y3[4]), .sel(Q2__Q1__Q0), .en(1'b1));  // open: out0, out1, out2
endmodule

module Busca_de_Yu (
  input  [1:0] Yu__Yd_Atuais,
  input  [3:0] O2d__O1u__O1d__O0u,
  input  [2:0] I2__I1__I0,
  input  [2:0] S2__S1__S0,
  output Yu
);

  wire and_1_out, and_2_out, or_1_out, or_2_out, or_3_out;

  or or_1 (or_1_out, I2__I1__I0[2], O2d__O1u__O1d__O0u[2], O2d__O1u__O1d__O0u[3]);
  or or_2 (or_2_out, or_1_out, I2__I1__I0[1], O2d__O1u__O1d__O0u[1]);
  and and_1 (and_1_out, or_2_out, S2__S1__S0[0]);
  or or_3 (or_3_out, and_1_out, and_2_out);
  and and_2 (and_2_out, or_1_out, S2__S1__S0[1]);
  and and_3 (Yu, ~Yu__Yd_Atuais[0], or_3_out);  // AND_Gate

  // Notes on the sheet:
  //   Yu = Yd' (S0 (O1d + O1u + O2d + I1 + I2) + S1 (O2d + O1u + I2))
endmodule

module Busca_de_Yd (
  input  [1:0] Yu__Yd_Atuais,
  input  [3:0] O2d__O1u__O1d__O0u,
  input  [2:0] I2__I1__I0,
  input  [2:0] S2__S1__S0,
  output Yd
);

  wire and_1_out, and_2_out, or_1_out, or_2_out, or_3_out;

  or or_1 (or_1_out, O2d__O1u__O1d__O0u[0], O2d__O1u__O1d__O0u[1], I2__I1__I0[0]);
  or or_2 (or_2_out, or_1_out, O2d__O1u__O1d__O0u[2], I2__I1__I0[1]);
  and and_1 (and_1_out, or_2_out, S2__S1__S0[2]);
  or or_3 (or_3_out, and_1_out, and_2_out);
  and and_2 (and_2_out, or_1_out, S2__S1__S0[1]);
  and and_3 (Yd, ~Yu__Yd_Atuais[1], or_3_out);  // AND_Gate

  // Notes on the sheet:
  //   Yd = Yu' (S2 (O1u + O1d + O0u + I1 + I0) + S1 (O1d + O0u + I0))
endmodule

module Entradas_para_7_Seg (
  input  [2:0] S2__S1__S0,
  output a,
  output b,
  output c,
  output d,
  output e,
  output f,
  output g
);

  not not_1 (a, S2__S1__S0[1]);
  not not_2 (c, S2__S1__S0[2]);
  not not_3 (d, S2__S1__S0[1]);
  not not_4 (e, S2__S1__S0[1]);

  assign b = 1'b1;
  assign f = S2__S1__S0[0];
  assign g = S2__S1__S0[2];
endmodule

module Entradas_para_Seta (
  input  [1:0] Yu__Yd,
  output [3:0] out_2,
  output [3:0] out_3,
  output [3:0] out_4
);

  or or_1 (out_3[0], Yu__Yd[1], Yu__Yd[0]);
  not not_1 (out_2[1], Yu__Yd[1]);
  not not_2 (out_4[1], Yu__Yd[1]);
  not not_3 (out_2[2], Yu__Yd[0]);
  not not_4 (out_4[2], Yu__Yd[0]);
  or or_2 (out_3[3], Yu__Yd[1], Yu__Yd[0]);

  assign {out_2[3], out_2[0]} = 2'b00;
  assign out_3[2:1] = 2'b11;
  assign {out_4[3], out_4[0]} = 2'b00;
endmodule

module Proximo_Andar (
  input  [2:0] Estado_Atual,
  input  [2:0] Destino,
  output [2:0] Proximo_Estado
);

  wire and_1_out, and_2_out, comparator_1_eq, comparator_2_eq, comparator_3_eq, comparator_4_eq, or_1_out;

  Comparator #(.width(3)) comparator_1 (.a(Estado_Atual), .b(3'b001), .eq(comparator_1_eq));  // open: gt, lt
  Comparator #(.width(3)) comparator_2 (.a(Destino), .b(3'b100), .eq(comparator_2_eq));  // open: gt, lt
  Comparator #(.width(3)) comparator_3 (.a(Estado_Atual), .b(3'b100), .eq(comparator_3_eq));  // open: gt, lt
  Comparator #(.width(3)) comparator_4 (.a(Destino), .b(3'b001), .eq(comparator_4_eq));  // open: gt, lt
  and and_1 (and_1_out, comparator_1_eq, comparator_2_eq);
  and and_2 (and_2_out, comparator_3_eq, comparator_4_eq);
  or or_1 (or_1_out, and_1_out, and_2_out);
  Multiplexer #(.width(3), .enable("false")) multiplexer_1 (
    .in0(Destino), .in1(3'b010), .out(Proximo_Estado), .sel(or_1_out));
endmodule
